# Fritzing sketch led(1) (saved by Fritzing 0.8.3b)
breadboards: 1

parts:
  Parte1 = Arduino Nano (Rev3.0)
  LED1 = LED - 5mm [color="Red (633nm)" package="5 mm [THT]"]

nets:
  N1: Parte1.GND, LED1.cathode
  N2: Parte1.D13/SCK, LED1.anode
