# Fritzing sketch led2 (saved by Fritzing 0.8.3b)
breadboards: 1

parts:
  Parte1 = Arduino Nano (Rev3.0)
  LED1 = LED - 5mm [color="Red (633nm)" package="5 mm [THT]"]
  LED2 = LED - 5mm [color="Red (633nm)" package="5 mm [THT]"]
  LED3 = LED - 5mm [color="Red (633nm)" package="5 mm [THT]"]

nets:
  N1: Parte1.GND, LED1.cathode, LED2.cathode, LED3.cathode
  N2: Parte1.D11/MOSI, LED3.anode
  N3: Parte1.D12/MISO, LED2.anode
  N4: Parte1.D13/SCK, LED1.anode
