# Fritzing sketch led3 (saved by Fritzing 0.8.3b)
breadboards: 1

parts:
  Parte1 = Arduino Uno (Rev3)
  SG1 = Buzzer 12mm [package=buzzer-ccv-kit]
  LED1 = LED - 5mm [color="Red (633nm)" package="5 mm [THT]"]
  LED2 = LED - 5mm [color="Red (633nm)" package="5 mm [THT]"]
  LED3 = LED - 5mm [color="Red (633nm)" package="5 mm [THT]"]
  LED4 = LED - 5mm [color="Red (633nm)" package="5 mm [THT]"]

nets:
  N1: Parte1.ICSP_MISO, Parte1.D12/MISO, LED2.anode
  N2: Parte1.ICSP_MOSI, Parte1.D11_PWM/MOSI, LED3.anode
  N3: Parte1.GND, SG1.1, LED1.cathode, LED2.cathode, LED3.cathode, LED4.cathode
  N4: Parte1.D9_PWM, SG1.2
  N5: Parte1.D10_PWM/SS, LED4.anode
  N6: Parte1.D13/SCK, LED1.anode
