# Fritzing sketch servo2 (saved by Fritzing 0.9.3b)
breadboards: 1

parts:
  Componente1 = Arduino Uno (Rev3)
  S1 = Pushbutton [package="[THT]"]
  J1 = Basic Servo

nets:
  N1: Componente1.D9_PWM, J1.pulse
  N2: Componente1.D2, S1.Pin_3, S1.Pin_4
  5V: Componente1.5V, J1.vcc
  GND: Componente1.GND, J1.gnd
  N3: S1.Pin_1, S1.Pin_2
